# Fritzing sketch marvin (saved by Fritzing 0.9.3b)
breadboards: 1

parts:
  LED1 = LED - 3mm [color="Red (633nm)" package="3 mm [THT]"]
  R1 = Resistor [tolerance=±5% resistance=100k package=THT]
  LED3 = LED - 3mm [color="Green (565nm)" package="3 mm [THT]"]
  LED2 = LED - 3mm [color="Yellow (585nm)" package="3 mm [THT]"]
  R2 = Resistor [tolerance=±5% resistance=220 package=THT]
  R3 = Resistor [tolerance=±5% resistance=220 package=THT]
  R4 = Resistor [tolerance=±5% resistance=220 package=THT]
  Part1 = Adafruit I2S Mic - SPH0645 [part_number="Adafruit #3421"]
  Part2 = Adafruit HUZZAH32 ESP32 Feather [part_number="Adafruit #3405"]
  Part3 = Adafruit MAX98357A I2S 3W Class D Amplifier [part_number="Adafruit #3006"]
  SP1 = SPEAKER [package=pcb_mount_speaker]

nets (from the schematic view):
  N1: LED1.cathode, R3.Pin_0
  N2: LED1.anode, Part2.A5_IO4
  VDD: R1.Pin_1, Part1.VDD, Part2.3.3V, Part3.VIN
  N3: LED3.cathode, R4.Pin_0
  N4: LED3.anode, Part2.A0_DAC2
  N5: LED2.cathode, R2.Pin_0
  N6: LED2.anode, Part2.A1_DAC1
  GND: R2.Pin_1, R3.Pin_1, R4.Pin_1, Part1.GND, Part2.GND
  N7: Part1.BCLK, Part2.IO13_A12
  N8: Part1.DATA, Part2.IO21
  N9: Part1.WS, Part2.IO15_A8
  N10: Part2.IO12_A11, Part3.LRCLK
  N11: Part2.IO27_A10, Part3.DIN
  N12: Part2.IO14_A6, Part3.BCLK
  N13: Part3.VO-, SP1.+
  N14: Part3.VO+, SP1.-

custom parts:
  Adafruit I2S Mic - SPH0645: For many microcontrollers, adding audio input is easy with one of our analog microphone breakouts. But as you get to bigger and better microcontrollers and microcomputers, you'll find that you don't always have an analog input, or maybe you want to avoid the noise that can seep in with an analog mic system. Once you get past 8-bit micros, you will often find an I2S peripheral, that can take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
  Adafruit MAX98357A I2S 3W Class D Amplifier: Listen to this good news - we now have an all in one digital audio amp breakout board that works incredibly well with the Raspberry Pi! If you're looking for an easy and low cost way to get you digital sound files bumpin' then the MAX08357 I2S Amp Breakout is for you. It takes standard I2S digital audio input and, not only decodes it into analog, but also amplifies it directly into a speaker.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
